# Fritzing sketch schematic2 (saved by Fritzing 1.0.0rc)
breadboards: 1

parts:
  I2C_SSD1315_128x64 = OLED 128x64 I2C Monochrome Display
  E3Z-R61 = E18-D80NK_1 [mn=or part_number="(NPN NO)" mpn=E3Z-LAS-R8 package=THT]
  S1 = Pushbutton [package="[THT]"]
  WeMos_D1_Mini1 = WeMos D1 Mini
  A1 = MH-FMD buzzer
  1-4_7kOm = Resistor [tolerance=±5% resistance=1 package="1206 [SMD]"]

nets:
  N1: I2C_SSD1315_128x64.GND, E3Z-R61.pin1, S1.Pin_1, S1.Pin_2, A1.Pin_3
  N2: E3Z-R61.pin2, A1.Pin_1
  N3: E3Z-R61.pin3, 1-4_7kOm.Pin_0
  N4: S1.Pin_3, S1.Pin_4
  N5: WeMos_D1_Mini1.RX, 1-4_7kOm.Pin_1

notes:
  +3V
  GND
  +5V
  You can power the entire board either through the MicroUSB port on the Wemos module or via the 5V and G (GND) pins.
  Active buzzer (D7 / GPIO 13) or Passive (D6 / GPIO 12)

custom parts:
  E18-D80NK_1: E18-D80NK Proximity Sensor module.
  MH-FMD buzzer: MH-FMD buzzer.
