# Fritzing sketch schematic4 (saved by Fritzing 1.0.0rc)
breadboards: 1

parts:
  I2C_SSD1315_128x64 = OLED 128x64 I2C Monochrome Display
  E3Z-R61 = E18-D80NK_1 [mn=or part_number="(NPN NO)" mpn=E3Z-LAS-R8 package=THT]
  Mod2 = Passive Buzzer
  S1 = Pushbutton [package="[THT]"]
  WeMos_D1_Mini1 = WeMos D1 Mini  # not connected
  1N4728A_3_3V = DIODE-ZENER [package=diode-zener]
  R2 = Resistor [tolerance=±5% resistance=10k package="2512 [SMD]"]
  DC_MINI_360 = Mini-360 DC-DC Buck converter [part_number="12v-23v to 5v" package=THT]
  R1 = Resistor [tolerance=±5% resistance=10k package="0402 [SMD]"]
  INPUT_12v-23v = Power plug

nets:
  N1: I2C_SSD1315_128x64.GND, E3Z-R61.pin1, Mod2.-, S1.Pin_1, S1.Pin_2, 1N4728A_3_3V.C, DC_MINI_360.OUT-
  N2: E3Z-R61.pin2, R2.Pin_1, DC_MINI_360.IN+, INPUT_12v-23v.VCC
  N3: E3Z-R61.pin3, R2.Pin_0
  N4: Mod2.S, DC_MINI_360.OUT+
  N5: S1.Pin_3, S1.Pin_4, R1.Pin_0
  N6: DC_MINI_360.IN-, INPUT_12v-23v.GND

notes:
  +3V
  GND
  +5V
  The laser sensor is powered directly from the power supply and requires a voltage of 10 to 23 volts. All other components are powered through the Mini 360 DC module, which should be configured to output 5 volts.

custom parts:
  E18-D80NK_1: E18-D80NK Proximity Sensor module.
  Mini-360 DC-DC Buck converter: Mini-360 DC-DC Buck converter. Tiny buck step down voltage converter, input voltage 4.75 to 23V output 1 to 17V adjustable. Available from ebay and the like.
