# Fritzing sketch schematic5 (saved by Fritzing 1.0.0rc)
breadboards: 1

parts:
  I2C_SSD1315_128x64 = OLED 128x64 I2C Monochrome Display
  E3Z-R61 = E18-D80NK_1 [mn=or mpn=E3Z-LAS-R8 part_number="(NPN NO)" package=THT]
  S1 = Pushbutton [package="[THT]"]
  A1 = MH-FMD buzzer
  A2 = Esp32-c3 super mini
  1-4_7kOm = Resistor [tolerance=±5% resistance=220 package="1206 [SMD]"]

nets:
  N1: I2C_SSD1315_128x64.SDA, A2.Pin_1
  N2: I2C_SSD1315_128x64.SCK, A2.Pin_13
  N3: I2C_SSD1315_128x64.VDD, A2.Pin_14
  N4: I2C_SSD1315_128x64.GND, E3Z-R61.pin1, S1.Pin_1, S1.Pin_2, A1.Pin_3, A2.Pin_15
  N5: E3Z-R61.pin2, A1.Pin_1, A2.Pin_16
  N6: E3Z-R61.pin3, 1-4_7kOm.Pin_1
  N7: S1.Pin_3, S1.Pin_4, A2.Pin_9
  N8: A1.Pin_2, A2.Pin_6
  N9: A2.Pin_12, 1-4_7kOm.Pin_0

notes:
  +5V
  GND
  You can power the entire board either through the MicroUSB port on the ESP32 module or via the 5V and GND pins.

custom parts:
  E18-D80NK_1: E18-D80NK Proximity Sensor module.
  MH-FMD buzzer: MH-FMD buzzer.
  Esp32-c3 super mini: ESP32-C3 Development Board ESP32 SuperMini Development Board ESP32 Development Board WiFi Bluetooth.
